// Logisim project duzy.circ as structural Verilog: 1 circuit, main circuit main
module main (
  input  reset,
  input  clock,
  input  stop,
  output [15:0] out_4,
  output [15:0] out_5,
  output [15:0] out_6,
  output [15:0] out_7,
  output [15:0] out_8,
  output [15:0] out_9,
  output [15:0] out_10,
  output [15:0] out_11,
  output [15:0] out_12,
  output [15:0] out_13,
  output [15:0] out_14,
  output [15:0] out_15,
  output [15:0] out_16,
  output [15:0] out_17,
  output [15:0] out_18,
  output [15:0] out_19,
  output [15:0] out_20,
  output [15:0] out_21,
  output [15:0] out_22,
  output [15:0] out_23,
  output [15:0] out_24,
  output [15:0] out_25,
  output [15:0] out_26,
  output [15:0] out_27,
  output [15:0] out_28,
  output [15:0] out_29,
  output [15:0] out_30,
  output [15:0] out_31,
  output [15:0] out_32,
  output [15:0] out_33,
  output [15:0] out_34,
  output [15:0] out_35,
  output _100,
  output _1000,
  output _10000
);

  wire and_1_out, counter_1_q, counter_3_q, main_1_p4, main_2_p5, main_3_p5, main_4_p5, main_5_p5, main_6_p5,
       main_7_p5, or_1_out, or_2_out, or_3_out;

  and and_1 (and_1_out, clock, ~stop);  // AND_Gate
  // wynik_wyświetlanie_mały_main main_1: pin names not known; wires that end beside it: out_4, out_5, out_6, main_1_p4, reset
  // wynik_wyświetlanie_mały_main main_2: pin names not known; wires that end beside it: main_1_p4, out_8, out_9, out_10, main_2_p5, reset
  // wynik_wyświetlanie_mały_main main_3: pin names not known; wires that end beside it: main_2_p5, out_12, out_13, out_14, main_3_p5, reset
  // wynik_wyświetlanie_mały_main main_4: pin names not known; wires that end beside it: main_3_p5, out_16, out_17, out_18, main_4_p5, reset
  // wynik_wyświetlanie_mały_main main_5: pin names not known; wires that end beside it: main_4_p5, out_20, out_21, out_22, main_5_p5, reset
  // wynik_wyświetlanie_mały_main main_6: pin names not known; wires that end beside it: main_5_p5, out_24, out_25, out_26, main_6_p5, reset
  or or_1 (or_1_out, stop, reset);
  Counter #(.width(1), .max('h1), .ongoal("stay")) counter_1 (
    .Q(counter_1_q), .clk(main_5_p5), .clr(or_2_out));  // open: load, D, count, carry
  or or_2 (or_2_out, main_4_p5, or_1_out);
  Counter #(.width(1), .max('h1), .ongoal("stay")) counter_2 (
    .Q(_10000), .clk(main_4_p5), .clr(or_1_out));  // open: load, D, count, carry
  Counter #(.width(1), .max('h1), .ongoal("stay")) counter_3 (
    .Q(counter_3_q), .clk(main_6_p5), .clr(or_3_out));  // open: load, D, count, carry
  or or_3 (or_3_out, main_5_p5, or_1_out);
  and and_2 (_100, counter_3_q, ~counter_1_q);  // AND_Gate
  and and_3 (_1000, counter_1_q, ~_10000);  // AND_Gate
  // wynik_wyświetlanie_mały_main main_7: pin names not known; wires that end beside it: main_6_p5, out_28, out_29, out_30, main_7_p5, reset
  // wynik_wyświetlanie_mały_main main_8: pin names not known; wires that end beside it: main_7_p5, out_32, out_33, out_34, and_1_out, reset

  assign out_7 = {16{1'b0}};
  assign out_11 = {16{1'b0}};
  assign out_15 = {16{1'b0}};
  assign out_19 = {16{1'b0}};
  assign out_23 = {16{1'b0}};
  assign out_27 = {16{1'b0}};
  assign out_31 = {16{1'b0}};
  assign out_35 = {16{1'b0}};
endmodule
