// Logisim project extrapatki.circ as structural Verilog: 1 circuit, main circuit main
module main (
  input  [31:0] dino_gora,
  input  [31:0] in_2,
  input  [31:0] in_3,
  input  [31:0] in_4,
  input  [31:0] dino_dol,
  input  clock,
  input  stop,
  input  ptak,
  input  clock_do_stopu,
  output [31:0] kolizja_1,
  output [31:0] kolizja_2,
  output [31:0] kolizja_3,
  output [31:0] kolizja_4,
  output [31:0] kolizja_5,
  output [31:0] gora,
  output [31:0] out_16,
  output [31:0] out_17,
  output [31:0] out_18,
  output [31:0] dol,
  output \łałanakła 
);

  wire and_1_out, counter_1_q, main_10_p10, not_1_out, not_2_out, not_3_out, not_4_out, not_5_out, not_6_out,
       not_7_out, not_8_out, not_9_out, not_10_out, not_11_out, or_1_out, or_2_out;
  wire [31:0] controlled_buffer_1_out, controlled_buffer_2_out, controlled_buffer_3_out,
       controlled_buffer_4_out, controlled_buffer_9_out, controlled_buffer_11_out, controlled_buffer_13_out,
       controlled_buffer_15_out, controlled_buffer_17_out, controlled_buffer_19_out, main_1_p9, main_2_p9,
       main_3_p9, main_4_p9, main_5_p9, main_6_p9, main_7_p9, main_8_p9, main_9_p9, main_10_p9;

  or or_1 (or_1_out, stop, ~ptak);  // OR_Gate
  and and_1 (and_1_out, clock, ptak);
  not not_1 (not_1_out, ptak);
  // kaktus_wyswietlanie_main main_1: pin names not known; wires that end beside it: {32{1'b0}}, {32{1'b0}}, {32{1'b0}}, {32{1'b0}}, {32{1'b0}}, {32{1'b0}}, and_1_out, or_1_out, main_1_p9
  // kaktus_wyswietlanie_main main_2: pin names not known; wires that end beside it: {32{1'b0}}, {32{1'b0}}, {32{1'b0}}, 32'h1, 32'h2, 32'h4, and_1_out, or_1_out, main_2_p9
  // kaktus_wyswietlanie_main main_3: pin names not known; wires that end beside it: {32{1'b0}}, 32'h3, 32'h6, 32'hc, 32'h18, 32'h30, and_1_out, or_1_out, main_3_p9
  // kaktus_wyswietlanie_main main_4: pin names not known; wires that end beside it: {32{1'b0}}, 32'h3, 32'h7, 32'hf, 32'h1f, 32'h3e, and_1_out, or_1_out, main_4_p9
  // kaktus_wyswietlanie_main main_5: pin names not known; wires that end beside it: {32{1'b0}}, 32'h1, 32'h3, 32'h7, 32'hf, 32'h1f, and_1_out, or_1_out, main_5_p9
  // kaktus_wyswietlanie_main main_6: pin names not known; wires that end beside it: {32{1'b0}}, 32'h1, 32'h3, 32'h7, 32'hf, 32'h1f, and_1_out, or_1_out, main_6_p9
  // kaktus_wyswietlanie_main main_7: pin names not known; wires that end beside it: {32{1'b0}}, {32{1'b0}}, 32'h1, 32'h3, 32'h7, 32'he, and_1_out, or_1_out, main_7_p9
  // kaktus_wyswietlanie_main main_8: pin names not known; wires that end beside it: {32{1'b0}}, {32{1'b0}}, {32{1'b0}}, {32{1'b0}}, {32{1'b0}}, {32{1'b0}}, and_1_out, or_1_out, main_8_p9
  // kaktus_wyswietlanie_main main_9: pin names not known; wires that end beside it: {32{1'b0}}, {32{1'b0}}, {32{1'b0}}, 32'h1, 32'h2, 32'h4, and_1_out, or_1_out, main_9_p9
  // kaktus_wyswietlanie_main main_10: pin names not known; wires that end beside it: {32{1'b0}}, {32{1'b0}}, {32{1'b0}}, {32{1'b0}}, {32{1'b0}}, {32{1'b0}}, and_1_out, or_1_out, main_10_p9, main_10_p10
  assign controlled_buffer_1_out = counter_1_q ? main_2_p9 : 32'bz;  // Controlled_Buffer controlled_buffer_1
  assign controlled_buffer_2_out = counter_1_q ? main_4_p9 : 32'bz;  // Controlled_Buffer controlled_buffer_2
  assign controlled_buffer_3_out = counter_1_q ? main_6_p9 : 32'bz;  // Controlled_Buffer controlled_buffer_3
  assign controlled_buffer_4_out = counter_1_q ? main_8_p9 : 32'bz;  // Controlled_Buffer controlled_buffer_4
  assign controlled_buffer_1_out = not_2_out ? main_1_p9 : 32'bz;  // Controlled_Buffer controlled_buffer_5
  not not_2 (not_2_out, counter_1_q);
  assign controlled_buffer_2_out = not_3_out ? main_3_p9 : 32'bz;  // Controlled_Buffer controlled_buffer_6
  not not_3 (not_3_out, counter_1_q);
  assign controlled_buffer_3_out = not_4_out ? main_5_p9 : 32'bz;  // Controlled_Buffer controlled_buffer_7
  not not_4 (not_4_out, counter_1_q);
  assign controlled_buffer_4_out = not_5_out ? main_7_p9 : 32'bz;  // Controlled_Buffer controlled_buffer_8
  not not_5 (not_5_out, counter_1_q);
  assign controlled_buffer_9_out = not_6_out ? main_9_p9 : 32'bz;  // Controlled_Buffer controlled_buffer_9
  not not_6 (not_6_out, counter_1_q);
  assign controlled_buffer_9_out = counter_1_q ? main_10_p9 : 32'bz;  // Controlled_Buffer controlled_buffer_10
  Counter #(.width(1), .max('h1)) counter_1 (.Q(counter_1_q), .clk(and_1_out));  // open: load, D, count, carry, clr
  not not_7 (not_7_out, or_2_out);
  assign controlled_buffer_11_out = or_2_out ? {32{1'b0}} : 32'bz;  // Controlled_Buffer controlled_buffer_11
  assign controlled_buffer_11_out = not_8_out ? controlled_buffer_2_out : 32'bz;  // Controlled_Buffer controlled_buffer_12
  not not_8 (not_8_out, or_2_out);
  assign controlled_buffer_13_out = or_2_out ? {32{1'b0}} : 32'bz;  // Controlled_Buffer controlled_buffer_13
  assign controlled_buffer_13_out = not_9_out ? controlled_buffer_3_out : 32'bz;  // Controlled_Buffer controlled_buffer_14
  not not_9 (not_9_out, or_2_out);
  assign controlled_buffer_15_out = or_2_out ? {32{1'b0}} : 32'bz;  // Controlled_Buffer controlled_buffer_15
  assign controlled_buffer_15_out = not_10_out ? controlled_buffer_4_out : 32'bz;  // Controlled_Buffer controlled_buffer_16
  not not_10 (not_10_out, or_2_out);
  assign controlled_buffer_17_out = or_2_out ? {32{1'b0}} : 32'bz;  // Controlled_Buffer controlled_buffer_17
  assign controlled_buffer_17_out = not_11_out ? controlled_buffer_9_out : 32'bz;  // Controlled_Buffer controlled_buffer_18
  not not_11 (not_11_out, or_2_out);
  or or_2 (or_2_out, or_1_out, not_1_out);
  assign controlled_buffer_19_out = or_2_out ? {32{1'b0}} : 32'bz;  // Controlled_Buffer controlled_buffer_19
  assign controlled_buffer_19_out = not_7_out ? controlled_buffer_1_out : 32'bz;  // Controlled_Buffer controlled_buffer_20
  and and_2 (\łałanakła , main_10_p10, ~not_1_out);  // AND_Gate
  // probaled2_main main_11: pin names not known; wires that end beside it: dino_gora, controlled_buffer_19_out, \łałanakła , clock_do_stopu, or_1_out, kolizja_1, gora
  // probaled2_main main_12: pin names not known; wires that end beside it: in_2, controlled_buffer_11_out, \łałanakła , clock_do_stopu, or_1_out, kolizja_2, out_16
  // probaled2_main main_13: pin names not known; wires that end beside it: in_3, controlled_buffer_13_out, \łałanakła , clock_do_stopu, or_1_out, kolizja_3, out_17
  // probaled2_main main_14: pin names not known; wires that end beside it: in_4, controlled_buffer_15_out, \łałanakła , clock_do_stopu, or_1_out, kolizja_4, out_18
  // probaled2_main main_15: pin names not known; wires that end beside it: dino_dol, controlled_buffer_17_out, \łałanakła , clock_do_stopu, or_1_out, kolizja_5, dol
endmodule
