// Logisim project imp.circ as structural Verilog: 1 circuit, main circuit main
module main (
);

  wire _32_out, _64_out, _128_out, _256_out, comparator_1_eq, comparator_2_eq, controlled_buffer_1_out,
       keyboard_1_avail, main_1_p5, main_1_p6, main_1_p7, main_1_p8, main_2_p2, main_2_p3, main_2_p4,
       main_2_p5, main_2_p6, main_3_p2, main_3_p4, main_3_p6, main_3_p8, main_3_p10, main_3_p12, main_3_p14,
       main_3_p17, main_3_p19, main_3_p21, main_3_p23, main_4_p2, main_4_p4, main_4_p6, main_4_p8,
       \reset_lub_wciśnij_klawisz_r_out , \skok_lub_wciśnij_spacje_out ;
  wire [6:0] keyboard_1_data;
  wire [31:0] main_4_p10, main_4_p11, main_4_p12, main_4_p13, main_4_p14, main_4_p15, main_4_p16, main_4_p17,
       main_4_p18, main_4_p19, main_4_p20, main_4_p21, main_4_p22, main_4_p23, main_4_p24, main_4_p25;

  Clock #(.highDuration(8), .lowDuration(8)) _32 (.out(_32_out));
  Clock #(.highDuration(4), .lowDuration(4)) _64 (.out(_64_out));
  Clock #(.highDuration(2), .lowDuration(2)) _128 (.out(_128_out));
  Clock _256 (.out(_256_out));
  // clock_zmiana_main main_1: pin names not known; wires that end beside it: _32_out, _64_out, _128_out, _256_out, main_1_p5, main_1_p6, main_1_p7, main_1_p8
  // mały_lub_duży_main main_2: pin names not known; wires that end beside it: main_1_p8, main_2_p2, main_2_p3, main_2_p4, main_2_p5, main_2_p6, main_2_p2, main_1_p8, main_2_p4, main_2_p3
  assign controlled_buffer_1_out = keyboard_1_avail ? main_1_p8 : 1'bz;  // Controlled_Buffer controlled_buffer_1
  Keyboard keyboard_1 (
    .clk(controlled_buffer_1_out), .avail(keyboard_1_avail), .data(keyboard_1_data));  // open: re, clr
  // przegrana_main main_3: pin names not known; wires that end beside it: main_2_p5, main_3_p2, main_3_p2, main_3_p4, main_3_p4, main_3_p6, main_3_p6, main_3_p8, main_3_p8, main_3_p10, main_3_p10, main_3_p12, main_3_p12, main_3_p14, main_3_p14, main_2_p2, main_3_p17, main_3_p17, main_3_p19, main_3_p19, main_3_p21, main_3_p21, main_3_p23
  // DotMatrix #(.matrixcols(32), .matrixrows(16)) dotmatrix_1: pin names not known; wires that end beside it: _32_out, main_2_p2, main_2_p5, main_1_p5, main_1_p6
  // skroceniev2_led_main main_4: pin names not known; wires that end beside it: main_3_p23, main_4_p2, main_4_p2, main_4_p4, main_4_p4, main_4_p6, main_4_p6, main_4_p8, main_4_p8, main_4_p10, main_4_p11, main_4_p12, main_4_p13, main_4_p14, main_4_p15, main_4_p16, main_4_p17, main_4_p18, main_4_p19, main_4_p20, main_4_p21, main_4_p22, main_4_p23, main_4_p24, main_4_p25
  DotMatrix #(.inputtype("row"), .matrixcols(32), .matrixrows(16)) dotmatrix_2 (
    .row0(main_4_p10), .row1(main_4_p11), .row2(main_4_p12), .row3(main_4_p13), .row4(main_4_p14),
    .row5(main_4_p15), .row6(main_4_p16), .row7(main_4_p17), .row8(main_4_p18), .row9(main_4_p19),
    .row10(main_4_p20), .row11(main_4_p21), .row12(main_4_p22), .row13(main_4_p23), .row14(main_4_p24),
    .row15(main_4_p25));
  Button \reset_lub_wciśnij_klawisz_r  (.out(\reset_lub_wciśnij_klawisz_r_out ));
  Comparator #(.width(7)) comparator_1 (.a(keyboard_1_data), .b(7'b0100000), .eq(comparator_1_eq));  // open: gt, lt
  Comparator #(.width(7)) comparator_2 (.a(keyboard_1_data), .b(7'b1110010), .eq(comparator_2_eq));  // open: gt, lt
  or or_1 (main_2_p6, comparator_1_eq, \skok_lub_wciśnij_spacje_out );
  or or_2 (main_2_p5, \reset_lub_wciśnij_klawisz_r_out , comparator_2_eq);
  Button \skok_lub_wciśnij_spacje  (.out(\skok_lub_wciśnij_spacje_out ));
  // wynik_wyświetlanie_duży_main main_5: pin names not known; wires that end beside it: main_1_p7
endmodule
