// Logisim project swi2led.circ as structural Verilog: 1 circuit, main circuit main
module main (
  input  guzik2,
  input  stop,
  input  clock,
  input  guzior,
  output [31:0] kolizja_wiersz_1,
  output [31:0] kolizja_wiersz_2,
  output [31:0] kolizja_wiersz_3,
  output [31:0] kolizja_wiersz_4,
  output [31:0] kolizja_wiersz_5,
  output [31:0] kolizja_wiersz_6,
  output [31:0] kolizja_wiersz_7,
  output [31:0] kolizja_wiersz_8,
  output [31:0] kolizja_wiersz_9,
  output [31:0] kolizja_wiersz_10,
  output [31:0] kolizja_wiersz_11,
  output [31:0] kolizja_wiersz_12,
  output [31:0] kolizja_wiersz_13,
  output [31:0] kolizja_wiersz_14,
  output [31:0] kolizja_wiersz_15,
  output [31:0] out_20,
  output [31:0] out_21,
  output [31:0] out_22,
  output [31:0] out_23,
  output [31:0] out_24,
  output [31:0] out_25,
  output [31:0] out_26,
  output [31:0] out_27,
  output [31:0] out_28,
  output [31:0] out_29,
  output [31:0] out_30,
  output [31:0] out_31,
  output [31:0] out_32,
  output [31:0] out_33,
  output [31:0] out_34,
  output [31:0] out_35,
  output ptak
);

  wire comparator_1_eq, comparator_2_eq, comparator_2_lt, d_ff_1_q, d_ff_1_qn, d_ff_2_q, d_ff_2_qn,
       main_1_p4, main_1_p5, main_1_p6, main_1_p7, main_1_p8, main_1_p9, main_1_p10, main_1_p11, main_1_p12,
       main_1_p13, main_1_p14, main_1_p15, main_1_p16, main_1_p17, main_1_p18, main_2_p9, main_2_p20,
       main_3_p10, main_4_p10, main_5_p10, not_1_out, not_2_out, not_3_out, not_4_out, not_5_out, or_1_out,
       xor_1_out;
  wire [1:0] random_1_out;
  wire [31:0] controlled_buffer_6_out, controlled_buffer_7_out, controlled_buffer_8_out,
       controlled_buffer_17_out, controlled_buffer_19_out, controlled_buffer_21_out,
       controlled_buffer_23_out, main_2_p15, main_2_p16, main_2_p17, main_2_p18, main_2_p19, main_3_p9,
       main_4_p9, main_5_p9, main_7_p7, main_8_p7;

  // dinozaur_wyswietlanie_main main_1: pin names not known; wires that end beside it: guzik2, clock, stop, main_1_p4, main_1_p5, main_1_p6, main_1_p7, main_1_p8, main_1_p9, main_1_p10, main_1_p11, main_1_p12, main_1_p13, main_1_p14, main_1_p15, main_1_p16, main_1_p17, main_1_p18, out_35
  Comparator #(.width(32), .mode("unsigned")) comparator_1 (
    .a(main_2_p17), .b({32{1'b0}}), .eq(comparator_1_eq));  // open: gt, lt
  Comparator #(.width(32), .mode("unsigned")) comparator_2 (
    .a({32{1'b0}}), .b(controlled_buffer_23_out), .eq(comparator_2_eq), .lt(comparator_2_lt));  // open: gt
  D_Flip_Flop d_ff_1 (
    .clk(comparator_1_eq), .D(d_ff_1_qn), .Q(d_ff_1_q), .Qn(d_ff_1_qn), .reset(xor_1_out));  // open: preset, en
  D_Flip_Flop d_ff_2 (
    .clk(comparator_2_eq), .D(d_ff_2_qn), .Q(d_ff_2_q), .Qn(d_ff_2_qn), .reset(xor_1_out));  // open: preset, en
  xor xor_1 (xor_1_out, d_ff_1_q, d_ff_2_q);
  and and_1 (ptak, random_1_out[0], random_1_out[1]);
  Random #(.width(2), .seed(23456765)) random_1 (.clk(xor_1_out), .out(random_1_out));  // open: next, clr
  // ptaki_main main_2: pin names not known; wires that end beside it: main_1_p5, main_1_p6, main_1_p7, main_1_p8, main_1_p9, clock, stop, ptak, main_2_p9, kolizja_wiersz_2, kolizja_wiersz_3, kolizja_wiersz_4, kolizja_wiersz_5, kolizja_wiersz_6, main_2_p15, main_2_p16, main_2_p17, main_2_p18, main_2_p19, main_2_p20
  assign out_21 = stop ? 32'h20c8af38 : 32'bz;  // Controlled_Buffer controlled_buffer_1
  assign out_21 = not_1_out ? main_2_p15 : 32'bz;  // Controlled_Buffer controlled_buffer_2
  assign out_22 = stop ? 32'h252ca840 : 32'bz;  // Controlled_Buffer controlled_buffer_3
  not not_1 (not_1_out, stop);
  assign out_22 = not_1_out ? main_2_p16 : 32'bz;  // Controlled_Buffer controlled_buffer_4
  assign out_27 = stop ? 32'h24c8af38 : 32'bz;  // Controlled_Buffer controlled_buffer_5
  assign controlled_buffer_6_out = not_1_out ? {32{1'b0}} : 32'bz;  // Controlled_Buffer controlled_buffer_6
  assign controlled_buffer_7_out = not_1_out ? {32{1'b0}} : 32'bz;  // Controlled_Buffer controlled_buffer_7
  assign controlled_buffer_8_out = not_1_out ? {32{1'b0}} : 32'bz;  // Controlled_Buffer controlled_buffer_8
  assign controlled_buffer_7_out = stop ? {32{1'b0}} : 32'bz;  // Controlled_Buffer controlled_buffer_9
  and and_2 (main_2_p9, clock, ~ptak);  // AND_Gate
  assign out_23 = stop ? 32'h292aa840 : 32'bz;  // Controlled_Buffer controlled_buffer_10
  assign out_25 = stop ? 32'h2929a840 : 32'bz;  // Controlled_Buffer controlled_buffer_11
  assign out_25 = not_1_out ? main_2_p19 : 32'bz;  // Controlled_Buffer controlled_buffer_12
  assign out_26 = stop ? 32'h2529a840 : 32'bz;  // Controlled_Buffer controlled_buffer_13
  assign out_23 = not_1_out ? main_2_p17 : 32'bz;  // Controlled_Buffer controlled_buffer_14
  assign out_24 = stop ? 32'h312aaf40 : 32'bz;  // Controlled_Buffer controlled_buffer_15
  assign out_24 = not_1_out ? main_2_p18 : 32'bz;  // Controlled_Buffer controlled_buffer_16
  // kaktus_wyswietlanie_main main_3: pin names not known; wires that end beside it: {32{1'b0}}, 32'h1, 32'h2, 32'h5, 32'ha, 32'h15, main_2_p9, stop, main_3_p9, main_3_p10
  or or_1 (or_1_out, main_2_p20, main_3_p10);
  // kaktus_wyswietlanie_main main_4: pin names not known; wires that end beside it: {32{1'b0}}, {32{1'b0}}, {32{1'b0}}, 32'h1, 32'h2, 32'h4, main_2_p9, stop, main_4_p9, main_4_p10, main_4_p10
  assign controlled_buffer_17_out = guzior ? main_4_p9 : 32'bz;  // Controlled_Buffer controlled_buffer_17
  // kaktus_wyswietlanie_main main_5: pin names not known; wires that end beside it: {32{1'b0}}, 32'h1, 32'h3, 32'h7, 32'hf, 32'h1f, main_2_p9, stop, main_5_p9, main_5_p10, main_5_p10, main_3_p10
  not not_2 (not_2_out, guzior);
  assign controlled_buffer_17_out = not_3_out ? main_3_p9 : 32'bz;  // Controlled_Buffer controlled_buffer_18
  not not_3 (not_3_out, guzior);
  assign controlled_buffer_19_out = guzior ? main_3_p9 : 32'bz;  // Controlled_Buffer controlled_buffer_19
  assign controlled_buffer_19_out = not_4_out ? main_5_p9 : 32'bz;  // Controlled_Buffer controlled_buffer_20
  not not_4 (not_4_out, guzior);
  assign controlled_buffer_21_out = guzior ? {32{1'b0}} : 32'bz;  // Controlled_Buffer controlled_buffer_21
  assign controlled_buffer_21_out = not_2_out ? main_4_p9 : 32'bz;  // Controlled_Buffer controlled_buffer_22
  assign controlled_buffer_23_out = guzior ? main_5_p9 : 32'bz;  // Controlled_Buffer controlled_buffer_23
  assign controlled_buffer_23_out = not_5_out ? main_4_p9 : 32'bz;  // Controlled_Buffer controlled_buffer_24
  not not_5 (not_5_out, guzior);
  // probaled2_main main_6: pin names not known; wires that end beside it: main_1_p4, {32{1'b0}}, stop, main_2_p9, stop, kolizja_wiersz_1, out_20
  // probaled2_main main_7: pin names not known; wires that end beside it: main_1_p10, controlled_buffer_8_out, or_1_out, main_2_p9, stop, kolizja_wiersz_7, main_7_p7, out_26
  // probaled2_main main_8: pin names not known; wires that end beside it: main_1_p11, controlled_buffer_6_out, or_1_out, main_2_p9, stop, kolizja_wiersz_8, main_8_p7, out_27
  // probaled2_main main_9: pin names not known; wires that end beside it: main_1_p12, controlled_buffer_7_out, or_1_out, main_2_p9, stop, kolizja_wiersz_9, out_28
  // probaled2_main main_10: pin names not known; wires that end beside it: main_1_p13, {32{1'b0}}, or_1_out, main_2_p9, stop, kolizja_wiersz_10, out_29
  // probaled2_main main_11: pin names not known; wires that end beside it: main_1_p14, controlled_buffer_21_out, or_1_out, main_2_p9, stop, kolizja_wiersz_11, out_30
  // probaled2_main main_12: pin names not known; wires that end beside it: controlled_buffer_17_out, main_1_p15, controlled_buffer_17_out, or_1_out, main_2_p9, stop, kolizja_wiersz_12, out_31
  // probaled2_main main_13: pin names not known; wires that end beside it: main_1_p16, controlled_buffer_19_out, or_1_out, main_2_p9, stop, kolizja_wiersz_13, out_32
  // probaled2_main main_14: pin names not known; wires that end beside it: main_1_p17, controlled_buffer_23_out, or_1_out, main_2_p9, stop, kolizja_wiersz_14, out_33
  // probaled2_main main_15: pin names not known; wires that end beside it: main_1_p18, main_4_p9, or_1_out, main_2_p9, stop, kolizja_wiersz_15, out_34
  assign out_26 = not_1_out ? main_7_p7 : 32'bz;  // Controlled_Buffer controlled_buffer_25
  assign out_27 = not_1_out ? main_8_p7 : 32'bz;  // Controlled_Buffer controlled_buffer_26
endmodule
